# Fritzing sketch rgb_light (saved by Fritzing 0.9.2b)
breadboards: 1

parts:
  U1 = NodeMCU V1.0
  Q1 = MOSFET-NCHANNEL [package=to220v]
  Q2 = MOSFET-NCHANNEL [package=to220v]
  Q3 = MOSFET-NCHANNEL [package=to220v]
  J2 = female pin header, 2 pins [form="♀ (female)"]
  J3 = male pin header, 4 pins [form="♂ (male)"]
  J5 = female pin header, 15 pins [form="♀ (female)"]
  J4 = female pin header, 15 pins [form="♀ (female)"]
  U2 = Voltage Regulator - 3.3V [package="TO220 [THT]"]
  C1 = Electrolytic Capacitor [capacitance=100µF voltage=50V package="100 mil [THT, electrolytic]"]
  C2 = Electrolytic Capacitor [capacitance=100µF voltage=50V package="100 mil [THT, electrolytic]"]

nets:
  N1: U1.D0, J4.pin1
  N2: U1.D1, J4.pin2
  N3: U1.D2, J4.pin3
  N4: U1.D3, J4.pin4
  N5: U1.D4, J4.pin5
  N6: U1.3V3, J5.pin11, J4.pin6, J4.pin15, U2.output_voltage, C1.+
  GND: U1.GND, Q1.S, Q2.S, Q3.S, J2.pin2, J5.pin10, J5.pin14, J4.pin7, J4.pin14, U2.GND, C1.-, C2.-
  N7: U1.D5, Q1.G, J4.pin8
  N8: U1.D6, Q2.G, J4.pin9
  N9: U1.D7, Q3.G, J4.pin10
  N10: U1.D8, J4.pin11
  N11: U1.RX, J4.pin12
  N12: U1.TX, J4.pin13
  N13: U1.Vin, J5.pin15
  N14: U1.RST, J5.pin13
  N15: U1.EN, J5.pin12
  N16: U1.CLK, J5.pin9
  N17: U1.SD0, J5.pin8
  N18: U1.CMD, J5.pin7
  N19: U1.SD1, J5.pin6
  N20: U1.SD2, J5.pin5
  N21: U1.SD3, J5.pin4
  N22: U1.RSV#40, J5.pin3
  N23: U1.RSV#41, J5.pin2
  N24: U1.A0, J5.pin1
  N25: Q1.D, J3.pin4
  N26: Q2.D, J3.pin3
  N27: Q3.D, J3.pin2
  N28: J2.pin1, J3.pin1, U2.input_voltage, C2.+

custom parts:
  NodeMCU V1.0: ESP8266 based NodeMCU
